# Fritzing sketch Desible_detection (saved by Fritzing 0.9.5d)
breadboards: 1

parts:
  LED2 = LED - 5mm [color="Red (633nm)" package="5 mm [THT]"]
  LED3 = LED - 5mm [color="Orange (620nm)" package="5 mm [THT]"]
  LED4 = LED - 5mm [color="Green (570nm)" package="5 mm [THT]"]
  Part1 = LCD1602-I2C
  U2 = 74HC4052 [package=dil16]
  Part3 = Breakout Board for Electret Microphone
  Part4 = Breakout Board for Electret Microphone
  Part5 = Breakout Board for Electret Microphone
  U3 = NodeMCU V3.0
  LED1 = LED - 5mm [color="Blue (525nm)" package="5 mm [THT]"]
  Part6 = Breakout Board for Electret Microphone
  S1 = Momentary Switch [package=ksa_sealed_tac_switch]
  S2 = Momentary Switch [package=ksa_sealed_tac_switch]
  R1 = Resistor [tolerance=±5% resistance=220 package=THT]
  R2 = Resistor [tolerance=±5% resistance=220 package=THT]
  J1 = Piezo Speaker
  A1 = ISD1820 module
  SP1 = SPEAKER [package=pcb_mount_speaker]

nets:
  N1: LED2.cathode, LED3.cathode, LED4.cathode, U3.GND#6, U3.GND#13, U3.GND#16, U3.GND#33, LED1.cathode, R1.Pin_1, R2.Pin_1, J1.pin1
  N2: LED2.anode, U3.D0
  N3: LED3.anode, U3.D6
  N4: LED4.anode, U3.D5
  GND: Part1.GND, Part5.GND
  VCC: Part1.VCC, Part5.VCC
  N5: Part1.SDA, U3.D2
  N6: Part1.SCL, U3.D1
  GND_2: U2.GND, U3.GND#41, Part6.GND, A1.Pin_2
  N7: U2.B, U3.S2
  N8: U2.A, U3.S3
  N9: U2.X3, Part5.AUD
  N10: U2.X0, Part4.AUD
  N11: U2.X, U3.A0
  N12: U2.X1, Part3.AUD
  N13: U2.X2, Part6.AUD
  N14: U2.VCC, U3.VU, A1.Pin_1
  N15: U3.D3, J1.pin2
  N16: U3.D4, LED1.anode
  N17: U3.3V3, S1.4, S2.4
  N18: U3.D7, S1.2, R1.Pin_0
  N19: U3.D8, S2.2, R2.Pin_0
  N20: U3.S1, A1.Pin_5
  N21: A1.Pin_13, SP1.-
  N22: A1.Pin_14, SP1.+

custom parts:
  LCD1602-I2C: A standard character display, usually with 2x16 characters. Comes in many colors with LCM1602 IIC attached.
  NodeMCU V3.0: ESP8266 based NodeMCU
  ISD1820 module: The ISD1820 is a record and playback module that can record a sound and play it whenever required.
